# Fritzing sketch Untitled Sketch 2 (saved by Fritzing 0.9.3b)

parts:
  S1 = H-Bridge with L298N
  Componente1 = Arduino Mega 2560 (Rev3)

nets:
  12V: S1.12V, Componente1.VIN
  GND: S1.GND, Componente1.GND

custom parts:
  H-Bridge with L298N: h-bridge
